# Fritzing sketch watering_array (saved by Fritzing 0.9.3b)
breadboards: 1

parts:
  WEMOS = WeMos D1 Mini
  R4 = Resistor [tolerance=±5% resistance=330 package=THT]
  V1 = DC Power [voltage=5V]
  P1 = Hirose DF13 Series Header [part_number=PUMP package=DF13C-2P-1.25V]
  D9 = Rectifier Diode [part_number=1N4001 package="300 mil [THT]"]
  TIP120 = TRANSISTOR_NPN [package=sot223]
  U11 = Hirose DF13 Series Header [part_number="SENSOR (moisturel)" package=DF13C-3P-1.25V]
  U12 = Hirose DF13 Series Header [part_number="LED (green / red)" package=DF13C-3P-1.25V]
  R7 = Resistor [tolerance=±5% resistance=470 package=THT]
  R8 = Resistor [tolerance=±5% resistance=470 package=THT]
  U10 = Hirose DF13 Series Header [part_number="SENSOR (water_tank)" package=DF13C-2P-1.25V]
  R9 = Resistor [tolerance=±5% resistance=10k package=THT]
  R11 = Trimmer Potentiometer [maximum_resistance=10kΩ package=THT]
  R12 = Resistor [tolerance=±5% resistance=10k package=THT]
  RESET = Pushbutton [package="[THT]"]

nets:
  N1: WEMOS.3V3, U11.1, U10.1, RESET.Pin_3, RESET.Pin_4
  N2: WEMOS.5V, V1.V+, P1.2, D9.cathode
  N3: WEMOS.A0, R11.wiper
  N4: WEMOS.D0, R12.Pin_1, RESET.Pin_1, RESET.Pin_2
  N5: WEMOS.D5, R7.Pin_0
  N6: WEMOS.D6, R8.Pin_0
  N7: WEMOS.D7, U10.2, R9.Pin_0
  N8: WEMOS.D8, R4.Pin_0
  N9: WEMOS.G, V1.V-, TIP120.E, U11.2, U12.2, R9.Pin_1, R11.leg1, R12.Pin_0
  N10: R4.Pin_1, TIP120.B
  N11: P1.1, D9.anode, TIP120.C
  N12: U11.3, R11.leg2
  N13: U12.1, R8.Pin_1
  N14: U12.3, R7.Pin_1

// code stored in the sketch: Untitled.ino

